// Logisim project alu.circ as structural Verilog: 3 circuits, main circuit alu
module alu (
  input  [31:0] A,
  input  [31:0] B,
  input  [3:0] ALUSel,
  output [31:0] Result
);

  wire [31:0] add0, and7, mul8, mulh9, mulhu11, or6, SLL1, slt2, sra13, srl5, sub12, xor4;

  SLT slt_1 (.SLTOut(slt2), .Ain(A), .Bin(B));
  Adder #(.width(32)) adder_1 (.a(A), .b(B), .out(add0));  // open: cin, cout
  Shifter #(.width(32)) shifter_1 (.in(A), .\dist (B[4:0]), .out(SLL1));
  assign xor4 = A ^ B;  // XOR_Gate xor_1, 32 bits wide
  Shifter #(.shift("lr"), .width(32)) shifter_2 (.in(A), .\dist (B[4:0]), .out(srl5));
  assign or6 = A | B;  // OR_Gate or_1, 32 bits wide
  assign and7 = A & B;  // AND_Gate and_1, 32 bits wide
  Subtractor #(.width(32)) subtractor_1 (.a(A), .b(B), .out(sub12));  // open: bin, bout
  Shifter #(.shift("ar"), .width(32)) shifter_3 (.in(A), .\dist (B[4:0]), .out(sra13));
  MyMultiplior mymultiplior_1 (.MULRES(mul8), .mulhuRES(mulhu11), .mulhRES(mulh9), .Ain(A), .Bin(B));
  Multiplexer #(.enable("false"), .select(4), .width(32)) multiplexer_1 (
    .in0(add0), .in1(SLL1), .in2(slt2), .in4(xor4), .in5(srl5), .in6(or6), .in7(and7), .in8(mul8),
    .in9(mulh9), .in11(mulhu11), .in12(sub12), .in13(sra13), .in15(B), .out(Result), .sel(ALUSel));  // open: in3, in10, in14

  // Other names for the same wires on the sheet: bsel15[31:0] = B

  // Notes on the sheet:
  //   INPUTS to your circuit
  //   DON'T CHANGE THE LOCATIONS OF THE INPUTS AND OUTPUTS!
  //   OUTPUT from your circuit
endmodule

module SLT (
  input  [31:0] Ain,
  input  [31:0] Bin,
  output [31:0] SLTOut
);

  wire and_1_out, and_2_out, not_1_out, not_2_out, xor_1_out;
  wire [31:0] subtractor_1_out;

  not not_1 (not_1_out, Bin[31]);
  and and_1 (and_1_out, Ain[31], not_1_out);
  Subtractor #(.width(32)) subtractor_1 (.a(Ain), .b(Bin), .out(subtractor_1_out));  // open: bin, bout
  xor xor_1 (xor_1_out, Ain[31], Bin[31]);
  not not_2 (not_2_out, xor_1_out);
  and and_2 (and_2_out, subtractor_1_out[31], not_2_out);
  or or_1 (SLTOut[0], and_1_out, and_2_out);

  assign SLTOut[31:1] = {31{1'b0}};
endmodule

module MyMultiplior (
  input  [31:0] Ain,
  input  [31:0] Bin,
  output [31:0] MULRES,
  output [31:0] mulhuRES,
  output [31:0] mulhRES
);

  wire [31:0] negator_1_out, negator_2_out, RES_01, RES_10, RES_11;

  Negator #(.width(32)) negator_1 (.in(Ain), .out(negator_1_out));
  Negator #(.width(32)) negator_2 (.in(Bin), .out(negator_2_out));
  Multiplier #(.width(32)) multiplier_1 (.a(negator_1_out), .b(negator_2_out), .cout(RES_11));  // open: out, cin
  Multiplier #(.width(32)) multiplier_2 (.a(Ain), .b(Bin), .out(MULRES), .cout(mulhuRES));  // open: cin
  Multiplier #(.width(32)) multiplier_3 (.a(Ain), .b({32{1'b1}}), .out(RES_10), .cin(mulhuRES));  // open: cout
  Multiplier #(.width(32)) multiplier_4 (.a(Bin), .b({32{1'b1}}), .out(RES_01), .cin(mulhuRES));  // open: cout
  Multiplexer #(.enable("false"), .select(2), .width(32)) multiplexer_1 (
    .in0(mulhuRES), .in1(RES_01), .in2(RES_10), .in3(RES_11), .out(mulhRES), .sel({Bin[31], Ain[31]}));

  // Other names for the same wires on the sheet: ASign = Ain[31]; INPUT1[31:0] = Ain; BSign = Bin[31];
  //   INPUT2[31:0] = Bin; RES_00[31:0] = mulhuRES
endmodule
