// Logisim project control-logic.circ as structural Verilog
module control_logic (
  input  [31:0] inst,
  input  BrEq,
  input  BrLt,
  input  PCSelS1,
  output PCSel,
  output RegWEn,
  output [2:0] ImmSel,
  output BrUn,
  output ASel,
  output BSel,
  output [3:0] ALUSel,
  output MemRW,
  output [1:0] WBSel,
  output CSRSel,
  output CSRWen
);

  wire add, addi, and_2_out, and_8_out, and_9_out, and_10_out, and_14_out, and_15_out, and_16_out,
       and_18_out, and_20_out, and_21_out, and_22_out, and_23_out, and_25_out, and_28_out, and_30_out,
       and_31_out, and_33_out, and_34_out, and_35_out, and_36_out, and_37_out, and_38_out, and_39_out,
       and_40_out, and_51_out, and_52_out, and_53_out, and_55_out, and_56_out, and_66_out, and_72_out,
       auipc_inst, csr_inst, csrw_inst, csrwi_inst, Eq0Lt1, Eq1Lt0, Fc3_Is_0, Fc3_Is_1, Fc3_Is_2, Fc3_Is_3,
       Fc3_Is_4, Fc3_Is_5, Fc3_Is_6, Fc3_Is_7, Fc7_Is_0, Fc7_Is_0x20, Fc7_Is_1, is_add0, is_and7, is_bsel15,
       is_mul8, is_mulh9, is_mulhu11, is_OPC_0x03, is_OPC_0x6f, is_OPC_0x13, is_OPC_0x67, is_or6, is_sll1,
       is_slt2, is_sra13, is_srl5, is_sub12, is_xor4, IType, lui_inst, nor_1_out, nor_2_out, not_1_out,
       not_2_out, not_5_out, not_6_out, not_7_out, not_8_out, not_9_out, not_10_out, not_11_out, not_12_out,
       not_13_out, not_14_out, not_16_out, not_17_out, not_18_out, not_19_out, not_20_out, not_21_out,
       not_22_out, not_23_out, not_24_out, not_25_out, not_26_out, not_27_out, not_28_out, not_29_out,
       not_30_out, not_31_out, not_32_out, not_33_out, not_34_out, not_35_out, not_36_out, not_37_out,
       NotRegWEn, op_high_is_6, op_low_is_3, OPC_isNot0, or_1_out, or_7_out, or_8_out, or_11_out, or_15_out,
       or_16_out, or_17_out, Pred_Right, priority_encoder_1_gs, priority_encoder_3_gs, R_and_I, RType,
       Rtype_fc3_is0, Rtype_fc3_is1, SBType, sll_inst, slli_inst, slt_inst, slti_inst, SType, UType,
       xor_1_out, xor_inst, xori_inst;
  wire [15:0] rom_1_data;

  or or_1 (or_1_out, is_OPC_0x67, is_OPC_0x6f);
  not not_1 (not_1_out, BrLt);
  not not_2 (not_2_out, BrEq);
  and and_1 (CSRWen, csr_inst, Pred_Right);
  not not_3 (BSel, RType);
  or or_2 (is_sll1, slli_inst, sll_inst);
  or or_3 (is_slt2, slti_inst, slt_inst);
  or or_4 (is_xor4, xor_inst, xori_inst);
  and and_2 (and_2_out, Fc3_Is_5, R_and_I);
  Priority_Encoder priority_encoder_1 (
    .in0(IType), .in1(SType), .in2(SBType), .in3(is_OPC_0x6f), .in4(UType), .out(ImmSel),
    .gs(priority_encoder_1_gs));  // open: in5, in6, in7, en_in, en_out
  // Probe on WBSel
  Priority_Encoder #(.select(2)) priority_encoder_2 (
    .in0(1'b1), .in1(is_OPC_0x03), .in2(csr_inst), .in3(or_1_out), .out(WBSel));  // open: gs, en_out, en_in
  and and_3 (Eq1Lt0, BrEq, not_1_out);
  and and_4 (Eq0Lt1, not_2_out, BrLt);
  xor xor_1 (xor_1_out, PCSel, PCSelS1);
  ROM #(.addrWidth(6), .dataWidth(16)) rom_1 (.data(rom_1_data));  // open: addr
  or or_5 (OPC_isNot0, inst[0], inst[1], inst[2], inst[3], inst[4], inst[5], inst[6]);
  and and_5 (MemRW, SType, Pred_Right);
  not not_4 (Pred_Right, xor_1_out);
  and and_6 (is_sra13, inst[30], and_2_out);
  and and_7 (is_srl5, and_2_out, Fc7_Is_0);
  or or_6 (is_add0, add, is_OPC_0x03, addi, SType, csrw_inst, SBType, auipc_inst, is_OPC_0x6f, is_OPC_0x67);
  not not_5 (not_5_out, BrLt);
  and and_8 (and_8_out, Eq1Lt0, Fc3_Is_0);
  or or_7 (or_7_out, Fc3_Is_4, Fc3_Is_6);
  not not_6 (not_6_out, BrEq);
  or or_8 (or_8_out, Fc3_Is_5, Fc3_Is_7);
  and and_9 (and_9_out, Eq0Lt1, or_7_out);
  and and_10 (and_10_out, Fc3_Is_1, not_6_out);
  or or_9 (R_and_I, RType, is_OPC_0x13);
  and and_11 (is_or6, Fc3_Is_6, R_and_I);
  and and_12 (is_and7, Fc3_Is_7, R_and_I);
  and and_13 (BrUn, inst[13], inst[14]);
  and and_14 (and_14_out, not_5_out, or_8_out);
  or or_10 (ASel, SBType, UType, is_OPC_0x6f);
  or or_11 (or_11_out, and_14_out, and_8_out, and_9_out, and_10_out);
  or or_12 (NotRegWEn, SBType, SType);
  not not_7 (not_7_out, NotRegWEn);
  and and_15 (and_15_out, or_11_out, SBType);
  and and_16 (and_16_out, inst[5], inst[4]);
  nor nor_1 (nor_1_out, inst[3], inst[2]);
  not not_8 (not_8_out, inst[3]);
  not not_9 (not_9_out, inst[6]);
  and and_17 (RegWEn, not_7_out, OPC_isNot0, Pred_Right);
  or or_13 (PCSel, and_15_out, is_OPC_0x67, is_OPC_0x6f);
  not not_10 (not_10_out, inst[4]);
  and and_18 (and_18_out, inst[5], inst[6]);
  not not_11 (not_11_out, inst[4]);
  not not_12 (not_12_out, inst[4]);
  not not_13 (not_13_out, inst[6]);
  or or_14 (is_bsel15, lui_inst, csrwi_inst);
  and and_19 (op_high_is_6, not_10_out, and_18_out);
  or or_15 (or_15_out, inst[2], inst[3]);
  not not_14 (not_14_out, inst[6]);
  and and_20 (and_20_out, and_16_out, nor_1_out);
  and and_21 (and_21_out, inst[5], inst[6]);
  and and_22 (and_22_out, op_low_is_3, not_12_out);
  and and_23 (and_23_out, inst[5], not_13_out);
  Priority_Encoder #(.select(4)) priority_encoder_3 (
    .in0(is_add0), .in1(is_sll1), .in2(is_slt2), .in4(is_xor4), .in5(is_srl5), .in6(is_or6), .in7(is_and7),
    .in8(is_mul8), .in9(is_mulh9), .in11(is_mulhu11), .in12(is_sub12), .in13(is_sra13), .in15(is_bsel15),
    .out(ALUSel), .gs(priority_encoder_3_gs));  // open: in3, in10, in14, en_out, en_in
  not not_15 (op_low_is_3, or_15_out);
  and and_24 (RType, not_14_out, and_20_out);
  and and_25 (and_25_out, op_low_is_3, not_11_out);
  and and_26 (SType, and_22_out, and_23_out);
  and and_27 (lui_inst, inst[2], not_8_out, inst[4], inst[5], not_9_out);
  and and_28 (and_28_out, inst[2], not_16_out);
  not not_16 (not_16_out, inst[3]);
  nor nor_2 (nor_2_out, inst[5], inst[6]);
  and and_29 (SBType, and_25_out, and_21_out);
  and and_30 (and_30_out, and_28_out, inst[4]);
  and and_31 (and_31_out, inst[2], inst[3]);
  and and_32 (auipc_inst, and_30_out, nor_2_out);
  not not_17 (not_17_out, inst[12]);
  not not_18 (not_18_out, inst[13]);
  not not_19 (not_19_out, inst[14]);
  not not_20 (not_20_out, inst[13]);
  not not_21 (not_21_out, inst[14]);
  not not_22 (not_22_out, inst[12]);
  not not_23 (not_23_out, inst[14]);
  not not_24 (not_24_out, inst[14]);
  not not_25 (not_25_out, inst[12]);
  not not_26 (not_26_out, inst[13]);
  not not_27 (not_27_out, inst[13]);
  not not_28 (not_28_out, inst[12]);
  or or_16 (or_16_out, inst[25], inst[26]);
  and and_33 (and_33_out, not_17_out, not_18_out);
  and and_34 (and_34_out, inst[12], not_20_out);
  and and_35 (and_35_out, not_22_out, inst[13]);
  and and_36 (and_36_out, inst[12], inst[13]);
  and and_37 (and_37_out, not_25_out, not_26_out);
  and and_38 (and_38_out, inst[12], not_27_out);
  and and_39 (and_39_out, not_28_out, inst[13]);
  and and_40 (and_40_out, inst[12], inst[13]);
  not not_29 (not_29_out, or_16_out);
  not not_30 (not_30_out, inst[30]);
  and and_41 (is_OPC_0x6f, and_31_out, op_high_is_6);
  not not_31 (not_31_out, inst[4]);
  or or_17 (or_17_out, inst[5], inst[6]);
  not not_32 (not_32_out, inst[3]);
  and and_42 (Fc3_Is_0, and_33_out, not_19_out);
  and and_43 (Fc3_Is_1, and_34_out, not_21_out);
  and and_44 (Fc3_Is_2, and_35_out, not_23_out);
  and and_45 (Fc3_Is_3, and_36_out, not_24_out);
  and and_46 (Fc3_Is_4, and_37_out, inst[14]);
  and and_47 (Fc3_Is_5, and_38_out, inst[14]);
  and and_48 (Fc3_Is_6, and_39_out, inst[14]);
  and and_49 (Fc3_Is_7, and_40_out, inst[14]);
  and and_50 (Fc7_Is_0, not_29_out, not_30_out);
  not not_33 (not_33_out, or_17_out);
  and and_51 (and_51_out, inst[2], not_32_out);
  and and_52 (and_52_out, op_low_is_3, not_31_out);
  and and_53 (and_53_out, op_low_is_3, inst[4]);
  and and_54 (is_OPC_0x67, and_51_out, op_high_is_6);
  and and_55 (and_55_out, op_low_is_3, inst[4]);
  and and_56 (and_56_out, inst[5], inst[6]);
  and and_57 (is_OPC_0x03, and_52_out, not_33_out);
  and and_58 (is_OPC_0x13, not_33_out, and_53_out);
  and and_59 (csr_inst, and_55_out, and_56_out);
  or or_18 (UType, auipc_inst, lui_inst);
  and and_60 (Rtype_fc3_is0, RType, Fc3_Is_0);
  not not_34 (not_34_out, inst[26]);
  not not_35 (not_35_out, inst[30]);
  or or_19 (IType, is_OPC_0x03, is_OPC_0x13, is_OPC_0x67, csr_inst);
  and and_61 (slli_inst, Fc3_Is_1, is_OPC_0x13);
  and and_62 (Rtype_fc3_is1, Fc3_Is_1, RType);
  and and_63 (slt_inst, RType, Fc3_Is_2);
  and and_64 (xor_inst, Fc3_Is_4, RType);
  and and_65 (xori_inst, Fc3_Is_4, is_OPC_0x13);
  and and_66 (and_66_out, inst[25], not_34_out);
  and and_67 (csrw_inst, csr_inst, Fc3_Is_1);
  and and_68 (csrwi_inst, csr_inst, Fc3_Is_5);
  and and_69 (add, Fc7_Is_0, Rtype_fc3_is0);
  and and_70 (addi, is_OPC_0x13, Fc3_Is_0);
  and and_71 (Fc7_Is_1, and_66_out, not_35_out);
  not not_36 (not_36_out, inst[25]);
  not not_37 (not_37_out, inst[26]);
  and and_72 (and_72_out, not_36_out, not_37_out);
  and and_73 (is_mul8, Fc7_Is_1, Rtype_fc3_is0);
  and and_74 (is_mulhu11, RType, Fc3_Is_3);
  and and_75 (sll_inst, Rtype_fc3_is1, Fc7_Is_0);
  and and_76 (is_mulh9, Rtype_fc3_is1, Fc7_Is_1);
  and and_77 (slti_inst, is_OPC_0x13, Fc3_Is_2);
  and and_78 (Fc7_Is_0x20, and_72_out, inst[30]);
  and and_79 (is_sub12, Fc7_Is_0x20, Rtype_fc3_is0);

  assign CSRSel = inst[14];

  // Other names for the same wires on the sheet: OP[6:0] = inst[6:0]; OPb0 = inst[0]; OPb1 = inst[1]; OPb2 = inst[2];
  //   OPb3 = inst[3]; OPb4 = inst[4]; OPb5 = inst[5]; OPb6 = inst[6]; rd[4:0] = inst[11:7]; Fc3_0 = inst[12];
  //   funct[2:0] = inst[14:12]; Fc3_1 = inst[13]; Fc3_2 = inst[14]; rs1[4:0] = inst[19:15];
  //   immShort[11:0] = inst[31:20]; rs2[4:0] = inst[24:20]; Fc7_0 = inst[25]; funct7[6:0] = inst[31:25];
  //   Fc7_1 = inst[26]; Fc7_5 = inst[30]; is_OPC_0x17 = auipc_inst; is_OPC_0x73 = csr_inst; jal_inst = is_OPC_0x6f;
  //   JType = is_OPC_0x6f; jalr_inst = is_OPC_0x67; load = is_OPC_0x03; mul_inst = is_mul8; mulh_inst = is_mulh9;
  //   mulhu_inst = is_mulhu11; sub_inst = is_sub12

  // Notes on the sheet:
  //   AUIPC
  //   jal
  //   jalr
  //   INPUTS to your circuit
  //   Imm-Sel
  //   MemRW
  //   WBSel
  //   CSRWen
  //   Connect ROM Input here ->
  //   BSEL
  //   RegWEn
  //   ROM FOR CONTROL LOGIC
  //   PCSel
  //   DON'T CHANGE THE LOCATIONS OF THE INPUTS AND OUTPUTS!
  //   OUTPUT from your circuit
  //   CLOSE
  //   WIRE
  //   TO
  //   USE
  //   ROM
  //   AluSel
  //   BrUn
  //   ASel
  //   CSRSel
  //   Reminder: Use combinational logic for PCSel
  //   0x63
  //   0x37
  //   0x23
  //   AUIPC
  //   jal
  //   jalr
  //   csr
  //   I_Type
endmodule
