// Logisim project cpu.circ as structural Verilog: 3 circuits, main circuit cpu
module cpu (
  input  clk,
  input  [31:0] INSTRUCTION,
  input  [31:0] READ_DATA,
  output [31:0] WRITE_ADDRESS,
  output [31:0] PROGRAM_COUNTER,
  output [31:0] ra,
  output [31:0] sp,
  output [31:0] t0,
  output [31:0] t1,
  output [31:0] t2,
  output [31:0] s0,
  output [31:0] s1,
  output [31:0] a0,
  output [31:0] tohost,
  output [3:0] WRITE_ENABLE,
  output [31:0] WRITE_DATA
);

  wire ASel, BrEq, BrLt, BrUn, BSel, csr_1_p6, CSRSel, CSRWen, MemRW, PCSel, RegWEn;
  wire [1:0] WBSel;
  wire [2:0] ImmSel;
  wire [3:0] ALUSel;
  wire [31:0] Immidiate, MemReadData, multiplexer_1_out, multiplexer_3_out, multiplexer_4_out,
       multiplexer_5_out, PCPlus4, rs1_data, rs2_data, WB_data;

  Adder #(.width(32)) adder_1 (.a(PROGRAM_COUNTER), .b(32'h4), .out(PCPlus4));  // open: cin, cout
  Multiplexer #(.enable("false"), .width(32)) multiplexer_1 (
    .in0(PCPlus4), .in1(WRITE_ADDRESS), .out(multiplexer_1_out), .sel(PCSel));
  Register #(.width(32)) PC (.D(multiplexer_1_out), .clk(clk), .Q(PROGRAM_COUNTER));  // open: en, clr
  Multiplexer #(.enable("false"), .select(2), .width(32)) multiplexer_2 (
    .in0(WRITE_ADDRESS), .in1(MemReadData), .in2(tohost), .in3(PCPlus4), .out(WB_data), .sel(WBSel));
  control_logic control_logic_1 (
    .CSRWen(CSRWen), .PCSel(PCSel), .RegWEn(RegWEn), .ImmSel(ImmSel), .BrUn(BrUn), .ASel(ASel), .BSel(BSel),
    .ALUSel(ALUSel), .MemRW(MemRW), .WBSel(WBSel), .CSRSel(CSRSel), .inst(INSTRUCTION), .BrEq(BrEq),
    .BrLt(BrLt));
  imm_gen imm_gen_1 (.inst(INSTRUCTION), .ImmSel(ImmSel), .imm(Immidiate));
  regfile regfile_1 (
    .rs1(INSTRUCTION[19:15]), .rs2(INSTRUCTION[24:20]), .rd(INSTRUCTION[11:7]), .Write_Data(WB_data),
    .RegWEn(RegWEn), .clk(clk), .ra(ra), .sp(sp), .t0(t0), .t1(t1), .t2(t2), .s0(s0), .s1(s1), .a0(a0),
    .Read_Data_1(rs1_data), .Read_Data_2(rs2_data));
  Multiplexer #(.enable("false"), .width(32)) multiplexer_3 (
    .in0(rs1_data), .in1({{27{1'b0}}, INSTRUCTION[19:15]}), .out(multiplexer_3_out), .sel(CSRSel));
  Multiplexer #(.enable("false"), .width(32)) multiplexer_4 (
    .in0(rs1_data), .in1(PROGRAM_COUNTER), .out(multiplexer_4_out), .sel(ASel));
  Multiplexer #(.enable("false"), .width(32)) multiplexer_5 (
    .in0(rs2_data), .in1(Immidiate), .out(multiplexer_5_out), .sel(BSel));
  alu alu_1 (.Result(WRITE_ADDRESS), .A(multiplexer_4_out), .B(multiplexer_5_out), .ALUSel(ALUSel));
  branch_comp branch_comp_1 (.rs1(rs1_data), .rs2(rs2_data), .BrUn(BrUn), .BrEq(BrEq), .BrLt(BrLt));
  // csr csr_1: pin names not known; wires that end beside it: INSTRUCTION[31:20], multiplexer_3_out, CSRWen, clk, tohost, csr_1_p6
  Mem_Write_Sub mem_write_sub_1 (
    .OPCode(INSTRUCTION[6:0]), .func3(INSTRUCTION[14:12]), .Address(WRITE_ADDRESS), .RS2(rs2_data),
    .MemWEn(WRITE_ENABLE), .MemData(WRITE_DATA));
  Mem_Read_Sub mem_read_sub_1 (
    .Extended_Data(MemReadData), .Read_Data(READ_DATA), .Func3(INSTRUCTION[14:12]), .Addr(WRITE_ADDRESS));

  // Other names for the same wires on the sheet: rs1[4:0] = INSTRUCTION[19:15]; alu_ans[31:0] = WRITE_ADDRESS;
  //   OP[6:0] = INSTRUCTION[6:0]; rd[4:0] = INSTRUCTION[11:7]; funct[2:0] = INSTRUCTION[14:12];
  //   csrAddr[11:0] = INSTRUCTION[31:20]; immShort[11:0] = INSTRUCTION[31:20]; rs2[4:0] = INSTRUCTION[24:20];
  //   funct7[6:0] = INSTRUCTION[31:25]

  // Notes on the sheet:
  //   Output to IMEM
  //   IMEM (do **NOT** move this)
  //   Inputs from IMEM
  //   It is OK to move the PC, RegFile, ALU, MEM, Branch Comp, Imm Gen, and Control Logic to wherever is most convenient for you when constructing your CPU, and to delete this text
  //   Inputs/Outputs for testing. Do **NOT** move these.
  //   Outputs To DMEM
  //   DMEM (do **NOT** move this)
  //   Inputs From DMEM
endmodule

module Mem_Write_Sub (
  input  [6:0] OPCode,
  input  [2:0] func3,
  input  [31:0] Address,
  input  [31:0] RS2,
  output [3:0] MemWEn,
  output [31:0] MemData
);

  wire and_1_out, and_2_out, and_4_out, and_5_out, and_7_out, and_8_out, and_9_out, and_10_out, and_11_out,
       and_12_out, and_13_out, and_14_out, and_15_out, f3_is_10, MemWEb0, MemWEb1, MemWEb2, MemWEb3,
       nor_1_out, not_2_out, not_3_out, not_4_out, not_5_out, not_6_out, not_7_out, not_8_out, not_9_out,
       not_11_out, not_12_out, not_13_out, not_14_out, not_15_out, not_16_out, not_17_out, not_18_out,
       not_19_out, not_20_out, not_21_out, not_22_out, or_1_out, or_4_out, Selb0, Selb1, SType, xor_1_out;

  // NOT_Gate not_1 has open pins: in=func3[0], out=open
  not not_2 (not_2_out, func3[1]);
  not not_3 (not_3_out, func3[0]);
  not not_4 (not_4_out, func3[1]);
  not not_5 (not_5_out, OPCode[2]);
  not not_6 (not_6_out, OPCode[3]);
  not not_7 (not_7_out, OPCode[4]);
  not not_8 (not_8_out, OPCode[6]);
  and and_1 (and_1_out, not_3_out, Address[0]);
  and and_2 (and_2_out, func3[0], not_4_out);
  and and_3 (SType, OPCode[0], OPCode[1], not_5_out, not_6_out, not_7_out, OPCode[5], not_8_out);
  xor xor_1 (xor_1_out, func3[0], Address[0]);
  and and_4 (and_4_out, not_2_out, Address[1]);
  or or_1 (or_1_out, and_1_out, and_2_out);
  not not_9 (not_9_out, func3[0]);
  and and_5 (and_5_out, xor_1_out, and_4_out);
  nor nor_1 (nor_1_out, func3[1], Address[1]);
  and and_6 (f3_is_10, not_9_out, func3[1]);
  or or_2 (MemWEb3, and_5_out, f3_is_10);
  and and_7 (and_7_out, or_1_out, nor_1_out);
  or or_3 (MemWEb1, and_7_out, f3_is_10);
  Multiplexer #(.enable("false"), .width(4)) multiplexer_1 (
    .in0(4'b0000), .in1({MemWEb3, MemWEb2, MemWEb1, MemWEb0}), .out(MemWEn), .sel(SType));
  Multiplexer #(.enable("false"), .select(2), .width(32)) multiplexer_2 (
    .in0({RS2[7:0], RS2[7:0], RS2[7:0], RS2[7:0]}), .in1({RS2[15:0], RS2[15:0]}),
    .in2({RS2[15:8], RS2[15:0], RS2[7:0]}), .in3(RS2), .out(MemData), .sel({Selb1, Selb0}));
  // NOT_Gate not_10 has open pins: in=func3[0], out=open
  not not_11 (not_11_out, func3[1]);
  not not_12 (not_12_out, Address[0]);
  not not_13 (not_13_out, Address[1]);
  not not_14 (not_14_out, func3[1]);
  not not_15 (not_15_out, Address[0]);
  not not_16 (not_16_out, Address[1]);
  not not_17 (not_17_out, func3[1]);
  not not_18 (not_18_out, Address[1]);
  not not_19 (not_19_out, func3[0]);
  not not_20 (not_20_out, func3[1]);
  not not_21 (not_21_out, Address[0]);
  not not_22 (not_22_out, func3[0]);
  and and_8 (and_8_out, not_12_out, Address[1]);
  and and_9 (and_9_out, func3[0], Address[0], not_13_out);
  and and_10 (and_10_out, not_14_out, not_15_out, not_16_out);
  and and_11 (and_11_out, func3[0], not_17_out, Address[0], not_18_out);
  and and_12 (and_12_out, not_19_out, func3[1]);
  and and_13 (and_13_out, func3[0], not_20_out, not_21_out);
  and and_14 (and_14_out, not_22_out, func3[1]);
  or or_4 (or_4_out, and_9_out, and_8_out);
  or or_5 (MemWEb0, and_10_out, f3_is_10);
  or or_6 (Selb1, and_11_out, and_12_out);
  or or_7 (Selb0, and_13_out, and_14_out);
  and and_15 (and_15_out, not_11_out, or_4_out);
  or or_8 (MemWEb2, and_15_out, f3_is_10);

  // Other names for the same wires on the sheet: b2 = Address[0]; b3 = Address[1]; b0 = func3[0]; b1 = func3[1];
  //   Out00[31:0] = {RS2[7:0], RS2[7:0], RS2[7:0], RS2[7:0]}; Out01_00n10[31:0] = {RS2[15:0], RS2[15:0]};
  //   Out01_01[31:0] = {RS2[15:8], RS2[15:0], RS2[7:0]}; RS2_00[7:0] = RS2[7:0]; RS2_01[7:0] = RS2[15:8];
  //   RS2_10[7:0] = RS2[23:16]; RS2_11[7:0] = RS2[31:24]

  // Notes on the sheet:
  //   !b1&b3(b0^!b2)+b1!b0
endmodule

module Mem_Read_Sub (
  input  [31:0] Read_Data,
  input  [2:0] Func3,
  input  [31:0] Addr,
  output [31:0] Extended_Data
);

  wire [31:0] Data00, Data01;

  Multiplexer #(.enable("false"), .select(2), .width(32)) multiplexer_1 (
    .in0(Data00), .in1(Data01), .in2(Read_Data), .out(Extended_Data), .sel(Func3[1:0]));  // open: in3
  Multiplexer #(.enable("false"), .select(2), .width(8)) multiplexer_2 (
    .in0(Read_Data[7:0]), .in1(Read_Data[15:8]), .in2(Read_Data[23:16]), .in3(Read_Data[31:24]),
    .out(Data00[7:0]), .sel(Addr[1:0]));
  Multiplexer #(.enable("false"), .select(2), .width(16)) multiplexer_3 (
    .in0(Read_Data[15:0]), .in1(Read_Data[23:8]), .in2(Read_Data[31:16]), .out(Data01[15:0]), .sel(Addr[1:0]));  // open: in3
  Multiplexer #(.enable("false"), .width(24)) multiplexer_4 (
    .in0({24{1'b0}}), .in1({24{1'b1}}), .out(Data00[31:8]), .sel(Data00[7]));
  Multiplexer #(.enable("false"), .width(16)) multiplexer_5 (
    .in0({16{1'b0}}), .in1({16{1'b1}}), .out(Data01[31:16]), .sel(Data01[15]));

  // Other names for the same wires on the sheet: DataB0[7:0] = Read_Data[7:0]; DataB1[7:0] = Read_Data[15:8];
  //   DataB2[7:0] = Read_Data[23:16]; DataB3[7:0] = Read_Data[31:24]; AddrLB2[1:0] = Addr[1:0]
endmodule
