// Logisim project cpu_backup.circ as structural Verilog: 7 circuits, main circuit cpu
module cpu (
  input  clk,
  input  [31:0] INSTRUCTION,
  input  [31:0] READ_DATA,
  output [31:0] WRITE_ADDRESS,
  output [31:0] PROGRAM_COUNTER,
  output [31:0] ra,
  output [31:0] sp,
  output [31:0] t0,
  output [31:0] t1,
  output [31:0] t2,
  output [31:0] s0,
  output [31:0] s1,
  output [31:0] a0,
  output [31:0] tohost,
  output [3:0] WRITE_ENABLE,
  output [31:0] WRITE_DATA
);

  wire ASel, BrEq, BrLt, BrUn, BSel, CSRSel, CSRWen, MemRW, not_1_out, PCSelS1, PCSelS2, RegWEn, RegWEn_LB;
  wire [1:0] WBSel;
  wire [2:0] funct, ImmSel;
  wire [3:0] ALUSel;
  wire [11:0] csrAddr;
  wire [19:0] Inst_S1;
  wire [31:0] Immidiate, MemReadData, multiplexer_1_out, multiplexer_3_out, multiplexer_4_out,
       multiplexer_5_out, PC_From_Register, PC_S1, PCp4_S1, PCPlus4, rs1_data, rs2_data, WB_data;

  Adder #(.width(32)) adder_1 (.a(PC_From_Register), .b(32'h4), .out(PCPlus4));  // open: cin, cout
  Multiplexer #(.enable("false"), .width(32)) multiplexer_1 (
    .in0(PCPlus4), .in1(WRITE_ADDRESS), .out(multiplexer_1_out));  // open: sel
  Register #(.width(32)) PC (.D(multiplexer_1_out), .clk(clk), .Q(PC_From_Register));  // open: en, clr
  IF_EXERegister if_exeregister_1 (
    .Instruction_Out({csrAddr, Inst_S1[19:15], funct, Inst_S1[11:0]}), .PC_Out(PC_S1), .PCplus4_Out(PCp4_S1),
    .PCSel_Out(PCSelS1), .CLk(clk), .Instruction(INSTRUCTION), .PC(PROGRAM_COUNTER), .PCplus4(PCPlus4),
    .PCSel(PCSelS2));
  Multiplexer #(.enable("false"), .select(2), .width(32)) multiplexer_2 (
    .in0(WRITE_ADDRESS), .in1(MemReadData), .in2(tohost), .in3(PCp4_S1), .out(WB_data), .sel(WBSel));
  regfile regfile_1 (
    .rs1(Inst_S1[19:15]), .rs2(csrAddr[4:0]), .rd(Inst_S1[11:7]), .Write_Data(WB_data), .RegWEn(RegWEn_LB),
    .clk(clk), .ra(ra), .sp(sp), .t0(t0), .t1(t1), .t2(t2), .s0(s0), .s1(s1), .a0(a0),
    .Read_Data_1(rs1_data), .Read_Data_2(rs2_data));
  imm_gen imm_gen_1 (.inst({csrAddr, Inst_S1[19:15], funct, Inst_S1[11:0]}), .ImmSel(ImmSel), .imm(Immidiate));
  not not_1 (not_1_out, clk);
  and and_1 (RegWEn_LB, not_1_out, RegWEn);
  Multiplexer #(.enable("false"), .width(32)) multiplexer_3 (
    .in0(rs1_data), .in1(PC_S1), .out(multiplexer_3_out), .sel(ASel));
  Multiplexer #(.enable("false"), .width(32)) multiplexer_4 (
    .in0(rs2_data), .in1(Immidiate), .out(multiplexer_4_out), .sel(BSel));
  Multiplexer #(.enable("false"), .width(32)) multiplexer_5 (
    .in0(rs1_data), .in1({{27{1'b0}}, Inst_S1[19:15]}), .out(multiplexer_5_out), .sel(CSRSel));
  branch_comp branch_comp_1 (.rs1(rs1_data), .rs2(rs2_data), .BrUn(BrUn), .BrEq(BrEq), .BrLt(BrLt));
  control_logic control_logic_1 (
    .CSRWen(CSRWen), .PCSel(PCSelS2), .RegWEn(RegWEn), .ImmSel(ImmSel), .BrUn(BrUn), .ASel(ASel),
    .BSel(BSel), .ALUSel(ALUSel), .MemRW(MemRW), .WBSel(WBSel), .CSRSel(CSRSel),
    .inst({csrAddr, Inst_S1[19:15], funct, Inst_S1[11:0]}), .PCSelS1(PCSelS1), .BrEq(BrEq), .BrLt(BrLt));
  alu alu_1 (.Result(WRITE_ADDRESS), .A(multiplexer_3_out), .B(multiplexer_4_out), .ALUSel(ALUSel));
  // csr csr_1: pin names not known; wires that end beside it: csrAddr, multiplexer_5_out, CSRWen, clk, tohost
  Mem_Write_Sub mem_write_sub_1 (
    .MemRW(MemRW), .func3(funct), .Address(WRITE_ADDRESS), .RS2(rs2_data), .MemWEn(WRITE_ENABLE),
    .MemData(WRITE_DATA));
  Mem_Read_Sub mem_read_sub_1 (.Extended_Data(MemReadData), .Read_Data(READ_DATA), .Func3(funct), .Addr(WRITE_ADDRESS));

  // Other names for the same wires on the sheet: rs1[4:0] = Inst_S1[19:15]; alu_ans[31:0] = WRITE_ADDRESS;
  //   alu_ans_S2[31:0] = WRITE_ADDRESS; OP[6:0] = Inst_S1[6:0]; rd[4:0] = Inst_S1[11:7];
  //   Inst_S1 (some bits) = {csrAddr, funct}; immShort[11:0] = csrAddr; rs2[4:0] = csrAddr[4:0];
  //   funct7[6:0] = csrAddr[11:5]

  // Notes on the sheet:
  //   Output to IMEM
  //   IMEM (do **NOT** move this)
  //   The postfix S1/S2 means this singnal is produced in S1/S2
  //   Inputs from IMEM
  //   Inputs/Outputs for testing. Do **NOT** move these.
  //   Outputs To DMEM
  //   DMEM (do **NOT** move this)
  //   Inputs From DMEM
endmodule

module Mem_Write_Sub (
  input  MemRW,
  input  [2:0] func3,
  input  [31:0] Address,
  input  [31:0] RS2,
  output [3:0] MemWEn,
  output [31:0] MemData
);

  wire and_1_out, and_2_out, and_3_out, and_4_out, and_6_out, and_7_out, and_8_out, and_9_out, and_10_out,
       and_11_out, and_12_out, and_13_out, and_14_out, f3_is_10, MemWEb0, MemWEb1, MemWEb2, MemWEb3,
       nor_1_out, not_2_out, not_3_out, not_4_out, not_5_out, not_7_out, not_8_out, not_9_out, not_10_out,
       not_11_out, not_12_out, not_13_out, not_14_out, not_15_out, not_16_out, not_17_out, not_18_out,
       or_1_out, or_4_out, Selb0, Selb1, xor_1_out;

  // NOT_Gate not_1 has open pins: in=func3[0], out=open
  not not_2 (not_2_out, func3[1]);
  not not_3 (not_3_out, func3[0]);
  not not_4 (not_4_out, func3[1]);
  and and_1 (and_1_out, not_3_out, Address[0]);
  and and_2 (and_2_out, func3[0], not_4_out);
  xor xor_1 (xor_1_out, func3[0], Address[0]);
  and and_3 (and_3_out, not_2_out, Address[1]);
  or or_1 (or_1_out, and_1_out, and_2_out);
  not not_5 (not_5_out, func3[0]);
  and and_4 (and_4_out, xor_1_out, and_3_out);
  nor nor_1 (nor_1_out, func3[1], Address[1]);
  and and_5 (f3_is_10, not_5_out, func3[1]);
  or or_2 (MemWEb3, and_4_out, f3_is_10);
  and and_6 (and_6_out, or_1_out, nor_1_out);
  or or_3 (MemWEb1, and_6_out, f3_is_10);
  Multiplexer #(.enable("false"), .width(4)) multiplexer_1 (
    .in0(4'b0000), .in1({MemWEb3, MemWEb2, MemWEb1, MemWEb0}), .out(MemWEn), .sel(MemRW));
  Multiplexer #(.enable("false"), .select(2), .width(32)) multiplexer_2 (
    .in0({RS2[7:0], RS2[7:0], RS2[7:0], RS2[7:0]}), .in1({RS2[15:0], RS2[15:0]}),
    .in2({RS2[15:8], RS2[15:0], RS2[7:0]}), .in3(RS2), .out(MemData), .sel({Selb1, Selb0}));
  // NOT_Gate not_6 has open pins: in=func3[0], out=open
  not not_7 (not_7_out, func3[1]);
  not not_8 (not_8_out, Address[0]);
  not not_9 (not_9_out, Address[1]);
  not not_10 (not_10_out, func3[1]);
  not not_11 (not_11_out, Address[0]);
  not not_12 (not_12_out, Address[1]);
  not not_13 (not_13_out, func3[1]);
  not not_14 (not_14_out, Address[1]);
  not not_15 (not_15_out, func3[0]);
  not not_16 (not_16_out, func3[1]);
  not not_17 (not_17_out, Address[0]);
  not not_18 (not_18_out, func3[0]);
  and and_7 (and_7_out, not_8_out, Address[1]);
  and and_8 (and_8_out, func3[0], Address[0], not_9_out);
  and and_9 (and_9_out, not_10_out, not_11_out, not_12_out);
  and and_10 (and_10_out, func3[0], not_13_out, Address[0], not_14_out);
  and and_11 (and_11_out, not_15_out, func3[1]);
  and and_12 (and_12_out, func3[0], not_16_out, not_17_out);
  and and_13 (and_13_out, not_18_out, func3[1]);
  or or_4 (or_4_out, and_8_out, and_7_out);
  or or_5 (MemWEb0, and_9_out, f3_is_10);
  or or_6 (Selb1, and_10_out, and_11_out);
  or or_7 (Selb0, and_12_out, and_13_out);
  and and_14 (and_14_out, not_7_out, or_4_out);
  or or_8 (MemWEb2, and_14_out, f3_is_10);

  // Other names for the same wires on the sheet: b2 = Address[0]; b3 = Address[1]; b0 = func3[0]; b1 = func3[1];
  //   Out00[31:0] = {RS2[7:0], RS2[7:0], RS2[7:0], RS2[7:0]}; Out01_00n10[31:0] = {RS2[15:0], RS2[15:0]};
  //   Out01_01[31:0] = {RS2[15:8], RS2[15:0], RS2[7:0]}; RS2_00[7:0] = RS2[7:0]; RS2_01[7:0] = RS2[15:8];
  //   RS2_10[7:0] = RS2[23:16]; RS2_11[7:0] = RS2[31:24]

  // Notes on the sheet:
  //   !b1&b3(b0^!b2)+b1!b0
endmodule

module Mem_Read_Sub (
  input  [31:0] Read_Data,
  input  [2:0] Func3,
  input  [31:0] Addr,
  output [31:0] Extended_Data
);

  wire [31:0] Data00, Data01;

  Multiplexer #(.enable("false"), .select(2), .width(32)) multiplexer_1 (
    .in0(Data00), .in1(Data01), .in2(Read_Data), .out(Extended_Data), .sel(Func3[1:0]));  // open: in3
  Multiplexer #(.enable("false"), .select(2), .width(8)) multiplexer_2 (
    .in0(Read_Data[7:0]), .in1(Read_Data[15:8]), .in2(Read_Data[23:16]), .in3(Read_Data[31:24]),
    .out(Data00[7:0]), .sel(Addr[1:0]));
  Multiplexer #(.enable("false"), .select(2), .width(16)) multiplexer_3 (
    .in0(Read_Data[15:0]), .in1(Read_Data[23:8]), .in2(Read_Data[31:16]), .out(Data01[15:0]), .sel(Addr[1:0]));  // open: in3
  Multiplexer #(.enable("false"), .width(24)) multiplexer_4 (
    .in0({24{1'b0}}), .in1({24{1'b1}}), .out(Data00[31:8]), .sel(Data00[7]));
  Multiplexer #(.enable("false"), .width(16)) multiplexer_5 (
    .in0({16{1'b0}}), .in1({16{1'b1}}), .out(Data01[31:16]), .sel(Data01[15]));

  // Other names for the same wires on the sheet: DataB0[7:0] = Read_Data[7:0]; DataB1[7:0] = Read_Data[15:8];
  //   DataB2[7:0] = Read_Data[23:16]; DataB3[7:0] = Read_Data[31:24]; AddrLB2[1:0] = Addr[1:0]
endmodule

module IF_EXERegister (
  input  [31:0] Instruction,
  input  [31:0] PC,
  input  [31:0] PCplus4,
  input  PCSel,
  input  CLk,
  output [31:0] Instruction_Out,
  output [31:0] PC_Out,
  output [31:0] PCplus4_Out,
  output PCSel_Out
);

  Register #(.width(32)) register_1 (.D(Instruction), .en(1'b1), .clk(CLk), .Q(Instruction_Out));  // open: clr
  Register #(.width(32)) register_2 (.D(PC), .en(1'b1), .clk(CLk), .Q(PC_Out));  // open: clr
  Register #(.width(32)) register_3 (.D(PCplus4), .en(1'b1), .clk(CLk), .Q(PCplus4_Out));  // open: clr
  Register #(.width(1)) register_4 (.D(PCSel), .en(1'b1), .clk(CLk), .Q(PCSel_Out));  // open: clr
endmodule

module safe_cpu (
);

  cpu cpu_1 ();  // open: clk, INSTRUCTION, READ_DATA, WRITE_ADDRESS, PROGRAM_COUNTER, ra, sp, t0, t1, t2, s0, s1, a0, tohost, WRITE_ENABLE, WRITE_DATA
endmodule

module EXE_IF_Register (
  input  [31:0] ALU_Answer,
  input  PCSel,
  input  clk,
  output [31:0] ALU_Ans_Out,
  output PCSel_Out
);

  Register #(.width(32)) register_1 (.D(ALU_Answer), .en(1'b1), .clk(clk), .Q(ALU_Ans_Out));  // open: clr
  Register #(.width(1)) register_2 (.D(PCSel), .en(1'b1), .clk(clk), .Q(PCSel_Out));  // open: clr
endmodule

module Mini_Decode (
  input  [31:0] Instruction,
  input  PCSelS2,
  input  PCSelS1,
  input  [31:0] Alu_ans_S2,
  input  [31:0] PCPlus4,
  input  [31:0] PC,
  output [31:0] NextPC
);
endmodule
