// Logisim project imm-gen.circ as structural Verilog: 1 circuit, main circuit imm_gen
module imm_gen (
  input  [31:0] inst,
  input  [2:0] ImmSel,
  output [31:0] imm
);

  wire [31:12] immB2, immI0, immS1;
  wire [31:20] immJ4;

  Multiplexer #(.enable("false"), .width(20)) multiplexer_1 (
    .in0({20{1'b0}}), .in1({20{1'b1}}), .out(immI0), .sel(inst[31]));
  Multiplexer #(.enable("false"), .select(3), .width(32)) multiplexer_2 (
    .in0({immI0, inst[31:20]}), .in1({immS1, inst[31:25], inst[11:7]}),
    .in2({immB2, inst[7], inst[30:25], inst[11:8], 1'b0}),
    .in3({immJ4, inst[19:12], inst[20], inst[30:21], 1'b0}), .in4({inst[31:12], {12{1'b0}}}), .out(imm),
    .sel(ImmSel));  // open: in5, in6, in7
  Multiplexer #(.enable("false"), .width(20)) multiplexer_3 (
    .in0({20{1'b0}}), .in1({20{1'b1}}), .out(immS1), .sel(inst[31]));
  Multiplexer #(.enable("false"), .width(12)) multiplexer_4 (
    .in0({12{1'b0}}), .in1({12{1'b1}}), .out(immJ4), .sel(inst[31]));
  Multiplexer #(.enable("false"), .width(20)) multiplexer_5 (
    .in0({20{1'b0}}), .in1({20{1'b1}}), .out(immB2), .sel(inst[31]));

  // Other names for the same wires on the sheet: immB2[11:1] = {inst[7], inst[30:25], inst[11:8]};
  //   immS1[11:0] = {inst[31:25], inst[11:7]}; rd[4:0] = inst[11:7]; funct[2:0] = inst[14:12];
  //   immJ4[19:1] = {inst[19:12], inst[20], inst[30:21]}; immU3[31:12] = inst[31:12]; rs1[4:0] = inst[19:15];
  //   immI0[11:0] = inst[31:20]; immShort[11:0] = inst[31:20]; high_bit = inst[31]; OP[6:0] = inst[6:0]

  // Notes on the sheet:
  //   INPUTS to your circuit
  //   DON'T CHANGE THE LOCATIONS OF THE INPUTS AND OUTPUTS!
  //   OUTPUT from your circuit
endmodule
