// Logisim project regfile.circ as structural Verilog: 5 circuits, main circuit regfile
module regfile (
  input  [4:0] rs1,
  input  [4:0] rs2,
  input  [4:0] rd,
  input  [31:0] Write_Data,
  input  RegWEn,
  input  clk,
  output [31:0] ra,
  output [31:0] sp,
  output [31:0] t0,
  output [31:0] t1,
  output [31:0] t2,
  output [31:0] s0,
  output [31:0] s1,
  output [31:0] a0,
  output [31:0] Read_Data_1,
  output [31:0] Read_Data_2
);

  wire demultiplexer_1_out0, demultiplexer_1_out1;
  wire [31:0] regs16a_1_dataout1, regs16a_1_dataout2, regs16b_1_dataout1, regs16b_1_dataout2;

  Demultiplexer #(.enable("false")) demultiplexer_1 (
    .out0(demultiplexer_1_out0), .out1(demultiplexer_1_out1), .in(RegWEn), .sel(rd[4]));
  regs16a regs16a_1 (
    .Write_Enable(demultiplexer_1_out0), .WriteAddr(rd[3:0]), .CLK(clk), .DataIn(Write_Data),
    .RegSel1(rs1[3:0]), .RegSel2(rs2[3:0]), .dataOUT1(regs16a_1_dataout1), .dataOUT2(regs16a_1_dataout2),
    .ra(ra), .sp(sp), .t0(t0), .t1(t1), .t2(t2), .s0(s0), .s1(s1), .a0(a0));
  regs16b regs16b_1 (
    .Write_Enable(demultiplexer_1_out1), .WriteAddr(rd[3:0]), .CLK(clk), .DataIn(Write_Data),
    .RegSel1(rs1[3:0]), .RegSel2(rs2[3:0]), .dataOUT1(regs16b_1_dataout1), .dataOUT2(regs16b_1_dataout2));
  Multiplexer #(.enable("false"), .width(32)) multiplexer_1 (
    .in0(regs16a_1_dataout1), .in1(regs16b_1_dataout1), .out(Read_Data_1), .sel(rs1[4]));
  Multiplexer #(.enable("false"), .width(32)) multiplexer_2 (
    .in0(regs16a_1_dataout2), .in1(regs16b_1_dataout2), .out(Read_Data_2), .sel(rs2[4]));

  // Other names for the same wires on the sheet: read_data1[31:0] = Read_Data_1; read_data2[31:0] = Read_Data_2;
  //   read_reg1[4:0] = rs1; rr1l[3:0] = rs1[3:0]; rr1h = rs1[4]; read_reg2[4:0] = rs2; rr2l[3:0] = rs2[3:0];
  //   rr2h = rs2[4]; write_en = RegWEn; write_reg[4:0] = rd; write_reg_low[3:0] = rd[3:0]; write_reg_hi = rd[4]

  // Notes on the sheet:
  //   INPUTS to your circuit
  //   DON'T CHANGE THE LOCATIONS OF THE INPUTS AND OUTPUTS!
  //   These are DEBUG/TEST outputs from your circuit.
  //   OUTPUTS from your circuit
endmodule

module regs4 (
  input  Write_Enable,
  input  [1:0] WriteAddr,
  input  CLK,
  input  [31:0] DataIn,
  input  [1:0] RegSel1,
  input  [1:0] RegSel2,
  output [31:0] dataOUT1,
  output [31:0] dataOUT2,
  output [31:0] reg00,
  output [31:0] reg01,
  output [31:0] reg10,
  output [31:0] reg11
);

  wire demultiplexer_1_out0, demultiplexer_1_out1, demultiplexer_1_out2, demultiplexer_1_out3;

  Demultiplexer #(.enable("false"), .select(2)) demultiplexer_1 (
    .out0(demultiplexer_1_out0), .out1(demultiplexer_1_out1), .out2(demultiplexer_1_out2),
    .out3(demultiplexer_1_out3), .in(Write_Enable), .sel(WriteAddr));
  Register #(.width(32)) register_1 (.D(DataIn), .en(demultiplexer_1_out0), .clk(CLK), .Q(reg00));  // open: clr
  Register #(.width(32)) register_2 (.D(DataIn), .en(demultiplexer_1_out1), .clk(CLK), .Q(reg01));  // open: clr
  Register #(.width(32)) register_3 (.D(DataIn), .en(demultiplexer_1_out2), .clk(CLK), .Q(reg10));  // open: clr
  Register #(.width(32)) register_4 (.D(DataIn), .en(demultiplexer_1_out3), .clk(CLK), .Q(reg11));  // open: clr
  Multiplexer #(.enable("false"), .select(2), .width(32)) multiplexer_1 (
    .in0(reg00), .in1(reg01), .in2(reg10), .in3(reg11), .out(dataOUT2), .sel(RegSel2));
  Multiplexer #(.enable("false"), .select(2), .width(32)) multiplexer_2 (
    .in0(reg00), .in1(reg01), .in2(reg10), .in3(reg11), .out(dataOUT1), .sel(RegSel1));

  // Other names for the same wires on the sheet: C = CLK; Din[31:0] = DataIn; OUT1[31:0] = dataOUT1;
  //   OUT2[31:0] = dataOUT2; RS1[1:0] = RegSel1; RS2[1:0] = RegSel2; WA[1:0] = WriteAddr; WE = Write_Enable
endmodule

module regs4a (
  input  Write_Enable,
  input  [1:0] WriteAddr,
  input  CLK,
  input  [31:0] DataIn,
  input  [1:0] RegSel1,
  input  [1:0] RegSel2,
  output [31:0] dataOUT1,
  output [31:0] dataOUT2,
  output [31:0] reg00,
  output [31:0] reg01,
  output [31:0] reg10,
  output [31:0] reg11
);

  wire demultiplexer_1_out1, demultiplexer_1_out2, demultiplexer_1_out3;

  Demultiplexer #(.enable("false"), .select(2)) demultiplexer_1 (
    .out1(demultiplexer_1_out1), .out2(demultiplexer_1_out2), .out3(demultiplexer_1_out3), .in(Write_Enable),
    .sel(WriteAddr));  // open: out0
  Register #(.width(32)) register_1 (.D(DataIn), .en(1'b0), .clk(CLK), .Q(reg00));  // open: clr
  Register #(.width(32)) register_2 (.D(DataIn), .en(demultiplexer_1_out1), .clk(CLK), .Q(reg01));  // open: clr
  Register #(.width(32)) register_3 (.D(DataIn), .en(demultiplexer_1_out2), .clk(CLK), .Q(reg10));  // open: clr
  Register #(.width(32)) register_4 (.D(DataIn), .en(demultiplexer_1_out3), .clk(CLK), .Q(reg11));  // open: clr
  Multiplexer #(.enable("false"), .select(2), .width(32)) multiplexer_1 (
    .in0(reg00), .in1(reg01), .in2(reg10), .in3(reg11), .out(dataOUT2), .sel(RegSel2));
  Multiplexer #(.enable("false"), .select(2), .width(32)) multiplexer_2 (
    .in0(reg00), .in1(reg01), .in2(reg10), .in3(reg11), .out(dataOUT1), .sel(RegSel1));

  // Other names for the same wires on the sheet: C = CLK; Din[31:0] = DataIn; OUT1[31:0] = dataOUT1;
  //   OUT2[31:0] = dataOUT2; RS1[1:0] = RegSel1; RS2[1:0] = RegSel2; WA[1:0] = WriteAddr; WE = Write_Enable
endmodule

module regs16a (
  input  Write_Enable,
  input  [3:0] WriteAddr,
  input  CLK,
  input  [31:0] DataIn,
  input  [3:0] RegSel1,
  input  [3:0] RegSel2,
  output [31:0] dataOUT1,
  output [31:0] dataOUT2,
  output [31:0] ra,
  output [31:0] sp,
  output [31:0] t0,
  output [31:0] t1,
  output [31:0] t2,
  output [31:0] s0,
  output [31:0] s1,
  output [31:0] a0
);

  wire demultiplexer_1_out0, demultiplexer_1_out1, demultiplexer_1_out2, demultiplexer_1_out3;
  wire [31:0] regs4_1_dataout1, regs4_1_dataout2, regs4_2_dataout1, regs4_2_dataout2, regs4_3_dataout1,
       regs4_3_dataout2, regs4a_1_dataout1, regs4a_1_dataout2;

  Demultiplexer #(.enable("false"), .select(2)) demultiplexer_1 (
    .out0(demultiplexer_1_out0), .out1(demultiplexer_1_out1), .out2(demultiplexer_1_out2),
    .out3(demultiplexer_1_out3), .in(Write_Enable), .sel(WriteAddr[3:2]));
  regs4a regs4a_1 (
    .dataOUT1(regs4a_1_dataout1), .dataOUT2(regs4a_1_dataout2), .reg01(ra), .reg10(sp),
    .RegSel1(RegSel1[1:0]), .RegSel2(RegSel2[1:0]), .Write_Enable(demultiplexer_1_out0), .CLK(CLK),
    .DataIn(DataIn), .WriteAddr(WriteAddr[1:0]));  // open: reg00, reg11
  regs4 regs4_1 (
    .dataOUT1(regs4_1_dataout1), .dataOUT2(regs4_1_dataout2), .reg01(t0), .reg10(t1), .reg11(t2),
    .RegSel1(RegSel1[1:0]), .RegSel2(RegSel2[1:0]), .Write_Enable(demultiplexer_1_out1), .CLK(CLK),
    .DataIn(DataIn), .WriteAddr(WriteAddr[1:0]));  // open: reg00
  regs4 regs4_2 (
    .dataOUT1(regs4_2_dataout1), .dataOUT2(regs4_2_dataout2), .reg00(s0), .reg01(s1), .reg10(a0),
    .RegSel1(RegSel1[1:0]), .RegSel2(RegSel2[1:0]), .Write_Enable(demultiplexer_1_out2), .CLK(CLK),
    .DataIn(DataIn), .WriteAddr(WriteAddr[1:0]));  // open: reg11
  regs4 regs4_3 (
    .dataOUT1(regs4_3_dataout1), .dataOUT2(regs4_3_dataout2), .RegSel1(RegSel1[1:0]), .RegSel2(RegSel2[1:0]),
    .Write_Enable(demultiplexer_1_out3), .CLK(CLK), .DataIn(DataIn), .WriteAddr(WriteAddr[1:0]));  // open: reg00, reg01, reg10, reg11
  Multiplexer #(.enable("false"), .select(2), .width(32)) multiplexer_1 (
    .in0(regs4a_1_dataout1), .in1(regs4_1_dataout1), .in2(regs4_2_dataout1), .in3(regs4_3_dataout1),
    .out(dataOUT1), .sel(RegSel1[3:2]));
  Multiplexer #(.enable("false"), .select(2), .width(32)) multiplexer_2 (
    .in0(regs4a_1_dataout2), .in1(regs4_1_dataout2), .in2(regs4_2_dataout2), .in3(regs4_3_dataout2),
    .out(dataOUT2), .sel(RegSel2[3:2]));

  // Other names for the same wires on the sheet: C = CLK; Din[31:0] = DataIn; OUT1[31:0] = dataOUT1;
  //   OUT2[31:0] = dataOUT2; RS1[3:0] = RegSel1; RS1L[1:0] = RegSel1[1:0]; RS1H[1:0] = RegSel1[3:2];
  //   RS2[3:0] = RegSel2; RS2L[1:0] = RegSel2[1:0]; RS2H[1:0] = RegSel2[3:2]; WA[3:0] = WriteAddr;
  //   WAL[1:0] = WriteAddr[1:0]; WAH[1:0] = WriteAddr[3:2]; WE = Write_Enable
endmodule

module regs16b (
  input  Write_Enable,
  input  [3:0] WriteAddr,
  input  CLK,
  input  [31:0] DataIn,
  input  [3:0] RegSel1,
  input  [3:0] RegSel2,
  output [31:0] dataOUT1,
  output [31:0] dataOUT2
);

  wire demultiplexer_1_out0, demultiplexer_1_out1, demultiplexer_1_out2, demultiplexer_1_out3;
  wire [31:0] regs4_1_dataout1, regs4_1_dataout2, regs4_2_dataout1, regs4_2_dataout2, regs4_3_dataout1,
       regs4_3_dataout2, regs4_4_dataout1, regs4_4_dataout2;

  Demultiplexer #(.enable("false"), .select(2)) demultiplexer_1 (
    .out0(demultiplexer_1_out0), .out1(demultiplexer_1_out1), .out2(demultiplexer_1_out2),
    .out3(demultiplexer_1_out3), .in(Write_Enable), .sel(WriteAddr[3:2]));
  regs4 regs4_1 (
    .dataOUT1(regs4_1_dataout1), .dataOUT2(regs4_1_dataout2), .RegSel1(RegSel1[1:0]), .RegSel2(RegSel2[1:0]),
    .Write_Enable(demultiplexer_1_out0), .CLK(CLK), .DataIn(DataIn), .WriteAddr(WriteAddr[1:0]));  // open: reg00, reg01, reg10, reg11
  regs4 regs4_2 (
    .dataOUT1(regs4_2_dataout1), .dataOUT2(regs4_2_dataout2), .RegSel1(RegSel1[1:0]), .RegSel2(RegSel2[1:0]),
    .Write_Enable(demultiplexer_1_out1), .CLK(CLK), .DataIn(DataIn), .WriteAddr(WriteAddr[1:0]));  // open: reg00, reg01, reg10, reg11
  regs4 regs4_3 (
    .dataOUT1(regs4_3_dataout1), .dataOUT2(regs4_3_dataout2), .RegSel1(RegSel1[1:0]), .RegSel2(RegSel2[1:0]),
    .Write_Enable(demultiplexer_1_out2), .CLK(CLK), .DataIn(DataIn), .WriteAddr(WriteAddr[1:0]));  // open: reg00, reg01, reg10, reg11
  regs4 regs4_4 (
    .dataOUT1(regs4_4_dataout1), .dataOUT2(regs4_4_dataout2), .RegSel1(RegSel1[1:0]), .RegSel2(RegSel2[1:0]),
    .Write_Enable(demultiplexer_1_out3), .CLK(CLK), .DataIn(DataIn), .WriteAddr(WriteAddr[1:0]));  // open: reg00, reg01, reg10, reg11
  Multiplexer #(.enable("false"), .select(2), .width(32)) multiplexer_1 (
    .in0(regs4_1_dataout1), .in1(regs4_2_dataout1), .in2(regs4_3_dataout1), .in3(regs4_4_dataout1),
    .out(dataOUT1), .sel(RegSel1[3:2]));
  Multiplexer #(.enable("false"), .select(2), .width(32)) multiplexer_2 (
    .in0(regs4_1_dataout2), .in1(regs4_2_dataout2), .in2(regs4_3_dataout2), .in3(regs4_4_dataout2),
    .out(dataOUT2), .sel(RegSel2[3:2]));

  // Other names for the same wires on the sheet: C = CLK; Din[31:0] = DataIn; OUT1[31:0] = dataOUT1;
  //   OUT2[31:0] = dataOUT2; RS1[3:0] = RegSel1; RS1L[1:0] = RegSel1[1:0]; RS1H[1:0] = RegSel1[3:2];
  //   RS2[3:0] = RegSel2; RS2L[1:0] = RegSel2[1:0]; RS2H[1:0] = RegSel2[3:2]; WA[3:0] = WriteAddr;
  //   WAL[1:0] = WriteAddr[1:0]; WAH[1:0] = WriteAddr[3:2]; WE = Write_Enable
endmodule
